# Fritzing sketch electronics Project - dsmart human rec (saved by Fritzing 0.9.3b)
circuit board: 8.46667cm x 5.64444cm
breadboards: 1

parts:
  IC1 = Rasberry Pi NIOR Camera [chip_label=IC package="DIP (Dual Inline) [THT]"]  # not connected
  J2 = Basic Servo
  J3 = Piezo Speaker
  J4 = Basic Servo
  Raspberry_Pi_1 = Raspberry Pi 3 [part_number=RPI-3-V1.2]
  X2 = USB Connectors [package=usb-minib-old]  # not connected
  Part1 = Arduino Mega 2560 (Rev3)
  Part2 = TFT 2.8 inch 320x240 Touch w microSD [part_number=1770]

nets:
  GND: J2.gnd, J3.pin1, J4.gnd, Raspberry_Pi_1.GND
  VCC: J2.vcc, J4.vcc, Raspberry_Pi_1.5V
  N1: J2.pulse, Raspberry_Pi_1.GPIO24
  N2: J3.pin2, Raspberry_Pi_1.GPIO15
  N3: J4.pulse, Raspberry_Pi_1.GPIO18
  3V3: Raspberry_Pi_1.3v3, Raspberry_Pi_1.3V3, Part1.3V3, Part2.x3
  N4: Part1.A0, Part2.LCD_D2
  N5: Part1.A1, Part2.LCD_D3
  N6: Part1.A2, Part2.LCD_D0
  N7: Part1.A3, Part2.LCD_D1
  N8: Part1.A4, Part2.LCD_RD, Part2.x8
  N9: Part1.A5, Part2.LCD_RS, Part2.x7
  N10: Part1.5V, Part2.x2
  N11: Part1.D0_RX0, Part2.LCD_D4
  N12: Part1.D1_TX0, Part2.LCD_D5
  N13: Part1.D2_PWM, Part2.LCD_D7
  N14: Part1.D3_PWM, Part2.LCD_D6
  N15: Part1.D4_PWM, Part2.SD_SS
  N16: Part1.D5_PWM, Part2.SD_DI
  N17: Part1.D6_PWM, Part2.SD_DO
  N18: Part1.D7_PWM, Part2.SD_SCK

custom parts:
  Rasberry Pi NIOR Camera: Camera
  TFT 2.8 inch 320x240 Touch w microSD: This TFT display is big (2.8" diagonal) bright (4 white-LED backlight) and colorful! 240x320 pixels with individual RGB pixel control. As a bonus, this display has a resistive touchscreen attached to it already, so you can detect finger presses anywhere on the screen.
