# Fritzing sketch electronics Project - smart human rec (saved by Fritzing 0.9.3b)
circuit board: 8.46667cm x 5.64444cm
breadboards: 1

parts:
  IC1 = Rasberry Pi NIOR Camera [chip_label=IC package="DIP (Dual Inline) [THT]"]  # not connected
  J2 = Basic Servo
  J3 = Piezo Speaker
  U1 = LCD-16X2 [package=lcd-16x2]
  J4 = Basic Servo
  Raspberry_Pi_1 = Raspberry Pi 3 [part_number=RPI-3-V1.2]
  X2 = USB Connectors [package=usb-minib-old]  # not connected

nets:
  GND: J2.gnd, J3.pin1, U1.VSS, U1.VO, U1.R_W, U1.K, J4.gnd, Raspberry_Pi_1.GND
  VCC: J2.vcc, J4.vcc, Raspberry_Pi_1.5V
  N1: J2.pulse, U1.VDD, U1.A, Raspberry_Pi_1.GPIO24
  N2: J3.pin2, Raspberry_Pi_1.GPIO15
  N3: U1.RS, Raspberry_Pi_1.GPIO26
  N4: U1.E, Raspberry_Pi_1.GPIO19
  N5: U1.DB4, Raspberry_Pi_1.GPIO13
  N6: U1.DB5, Raspberry_Pi_1.GPIO6
  N7: U1.DB6, Raspberry_Pi_1.GPIO5
  N8: U1.DB7, Raspberry_Pi_1.GPIO11
  N9: J4.pulse, Raspberry_Pi_1.GPIO18

custom parts:
  Rasberry Pi NIOR Camera: Camera

// code stored in the sketch: New FIle.ino

